# Fritzing sketch AmbienteSaudavel (saved by Fritzing 0.9.3b)
breadboards: 1

parts:
  R1 = Resistor [tolerance=±5% resistance=220 package=THT]
  Componente1 = Arduino Uno (Rev3) - ICSP
  RHT1 = Humidity and Temperature Sensor RHT03
  U1 = LCD-16X2 [package=lcd-16x2_noholes]
  LCM1602_IIC1 = LCM1602 IIC [part_number="LCM1602 IIC" chip_label="LCM1602 IIC" package="DIP (Dual Inline) [THT]"]
  U2 = 2-Channel 5v Relay Shield [package=relay-2ch5v10a]

nets:
  VCC: R1.Pin_0, Componente1.5V, RHT1.Vcc, LCM1602_IIC1.VCC, U2.VCC
  N1: R1.Pin_1, Componente1.A0, RHT1.Data-signal
  N2: Componente1.A4/SDA, LCM1602_IIC1.SCL
  N3: Componente1.A5/SCL, LCM1602_IIC1.SDA
  N4: Componente1.D2, U2.IN2
  N5: Componente1.D3_PWM, U2.IN1
  GND: Componente1.GND, RHT1.GND_2, LCM1602_IIC1.GND, U2.GND
  VSS: U1.VSS, LCM1602_IIC1.VSS
  VDD: U1.VDD, LCM1602_IIC1.VDD
  N6: U1.VO, U1.RS, LCM1602_IIC1.V0, LCM1602_IIC1.RS
  N7: U1.R_W, LCM1602_IIC1.RW
  N8: U1.E, LCM1602_IIC1.E
  N9: U1.DB0, LCM1602_IIC1.D0
  N10: U1.DB1, LCM1602_IIC1.D1
  N11: U1.DB2, LCM1602_IIC1.D2
  N12: U1.DB3, LCM1602_IIC1.D3
  N13: U1.DB4, LCM1602_IIC1.D4
  N14: U1.DB5, LCM1602_IIC1.D5
  N15: U1.DB6, LCM1602_IIC1.D6
  N16: U1.DB7, LCM1602_IIC1.D7
  N17: U1.A, LCM1602_IIC1.A
  N18: U1.K, LCM1602_IIC1.K

custom parts:
  LCM1602 IIC: I2C-Module to use a 1602 or 2004 LCD on with the wire.h libory Serial LCD Modul
  2-Channel 5v Relay Shield: 2 Channel 5v Relay Shield w. 2x SPD-06VDC-SD-C
